// Logisim project Q28BITFULLADDER.circ as structural Verilog: 1 circuit, main circuit main
module main (
  input  [7:0] in_1,
  input  [7:0] in_2,
  input  [7:0] in_3,
  output [7:0] out_4,
  output [7:0] out_5
);

  wire [7:0] and_1_out, and_2_out, xor_1_out;

  assign xor_1_out = in_1 ^ in_2;  // XOR_Gate xor_1, 8 bits wide
  assign and_1_out = in_1 & in_2;  // AND_Gate and_1, 8 bits wide
  assign out_4 = xor_1_out ^ in_3;  // XOR_Gate xor_2, 8 bits wide
  assign and_2_out = xor_1_out & in_3;  // AND_Gate and_2, 8 bits wide
  assign out_5 = and_2_out | and_1_out;  // OR_Gate or_1, 8 bits wide

  // Notes on the sheet:
  //   adham Oudeif
endmodule
