// Logisim project QUESTION4.circ as structural Verilog: 1 circuit, main circuit main
module main (
  input  [7:0] in_1,
  input  [7:0] in_2,
  input  [7:0] in_3,
  input  [2:0] in_4,
  input  in_5,
  output out_6
);

  wire [7:0] adder_1_out, and_1_out, bitadder_1_out, nand_1_out, negator_1_out, nor_1_out, not_1_out,
       or_1_out, subtractor_1_out, xor_1_out;
  wire [7:1] undriven;

  assign not_1_out = ~in_1;  // NOT_Gate not_1, 8 bits wide
  Negator negator_1 (.in(in_1), .out(negator_1_out));
  assign or_1_out = in_1 | in_1;  // OR_Gate or_1, 8 bits wide
  assign and_1_out = in_1 & in_1;  // AND_Gate and_1, 8 bits wide
  Adder adder_1 (.a(in_1), .b(in_1), .out(adder_1_out));  // open: cin, cout
  Subtractor subtractor_1 (.a(in_1), .b(in_1), .out(subtractor_1_out));  // open: bin, bout
  assign nand_1_out = ~(in_1 & in_1);  // NAND_Gate nand_1, 8 bits wide
  assign nor_1_out = ~(in_1 | in_1);  // NOR_Gate nor_1, 8 bits wide
  assign xor_1_out = in_1 ^ in_1;  // XOR_Gate xor_1, 8 bits wide
  Multiplexer #(.select(3), .width(8)) multiplexer_1 (
    .in0(negator_1_out), .in1(or_1_out), .in2(adder_1_out), .in3(subtractor_1_out), .in4(nand_1_out),
    .in5(nor_1_out), .in6(xor_1_out), .in7(and_1_out), .out(in_2), .sel(in_4));  // open: en
  BitAdder bitadder_1 (.in0(in_2), .out(bitadder_1_out[3:0]));
  Comparator comparator_1 (.a(bitadder_1_out), .b({undriven, in_5}), .eq(out_6));  // open: gt, lt
  // Pins of 4 and 8 bits meet at bitadder_1_out
  // Pins of 1 and 8 bits meet at {undriven, in_5}

  assign in_3 = in_1;

  // Notes on the sheet:
  //   Q4 FROM BOOK
endmodule
