// Logisim project Queston1.circ as structural Verilog: 1 circuit, main circuit main
module main (
  input  in_1,
  input  in_2,
  input  in_3,
  input  in_4,
  input  in_5,
  output out_6,
  output out_7,
  output out_8,
  output out_9,
  output out_10,
  output out_11,
  output out_12
);

  wire and_1_out, and_2_out, and_3_out, and_4_out, and_5_out, and_6_out, and_7_out, and_8_out, and_9_out,
       and_10_out, and_11_out, and_12_out, and_13_out, and_14_out, and_15_out, and_16_out, and_17_out,
       buffer_2_out, nand_1_out, nand_4_out, not_1_out, undriven, undriven_2, undriven_3;

  not not_1 (not_1_out, in_1);
  not not_2 (not_1_out, in_2);
  not not_3 (not_1_out, in_3);
  not not_4 (not_1_out, in_4);
  buf buffer_1 (not_1_out, in_5);
  nand nand_1 (nand_1_out, not_1_out, not_1_out);
  // NAND_Gate nand_2 has open pins: in0=not_1_out, in4=not_1_out, out=open
  // NAND_Gate nand_3 has open pins: in0=not_1_out, in4=not_1_out, out=open
  nand nand_4 (nand_4_out, not_1_out, not_1_out);
  and and_1 (and_1_out, undriven, nand_4_out);
  and and_2 (and_2_out, not_1_out, undriven_2);
  and and_3 (and_3_out, nand_1_out, not_1_out, undriven_2, undriven_3);
  and and_4 (and_4_out, undriven, nand_4_out);
  and and_5 (and_5_out, nand_1_out, undriven_2, undriven_2);
  and and_6 (and_6_out, undriven_2, undriven_3);
  and and_7 (and_7_out, not_1_out, undriven, undriven_2);
  and and_8 (and_8_out, nand_1_out, undriven, undriven_2);
  and and_9 (and_9_out, nand_1_out, not_1_out, undriven);
  and and_10 (and_10_out, not_1_out, undriven, undriven_2);
  and and_11 (and_11_out, nand_1_out, not_1_out, undriven_2);
  buf buffer_2 (buffer_2_out, nand_1_out);
  and and_12 (and_12_out, undriven, undriven_2);
  and and_13 (and_13_out, nand_1_out, not_1_out);
  and and_14 (and_14_out, not_1_out, undriven_2);
  and and_15 (and_15_out, nand_1_out, undriven_2, undriven_3);
  and and_16 (and_16_out, nand_1_out, nand_1_out, undriven, undriven_2);
  and and_17 (and_17_out, not_1_out, undriven_2, undriven_3);
  nor nor_1 (out_6, and_1_out, and_2_out, and_3_out);
  nor nor_2 (out_7, and_4_out, and_5_out, and_6_out);
  nor nor_3 (out_8, and_7_out, and_8_out);
  nor nor_4 (out_9, and_9_out, and_10_out, and_11_out);
  nor nor_5 (out_10, buffer_2_out, and_12_out);
  nor nor_6 (out_11, and_13_out, and_14_out, and_15_out);
  nor nor_7 (out_12, and_16_out, and_17_out);
  _7_Segment_Display u_7_segment_display_1 ();  // open: g, f, a, b, e, d, c, dp
  _7_Segment_Display u_7_segment_display_2 (
    .g(out_12), .f(out_11), .a(out_6), .b(out_7), .e(out_10), .d(out_8), .dp(out_9));  // open: c
endmodule
